# Fritzing sketch storymaker_breadboard (saved by Fritzing 1.0.4)
breadboards: 1

parts:
  Part1 = NRF24L01+ Breakout Board
  Part2 = Arduino Nano (Rev3.0)
  S1 = Pushbutton [package="[THT]"]
  C1 = Capacitor [package=cap-pth-small2]
  S2 = 0.91 inch OLED I2C Display 128 x 32 Pixels

nets:
  GND: Part1.GND, Part2.GND, S1.Pin_1, S1.Pin_2, C1.2, S2.GND
  VCC: Part1.VCC, Part2.3V3
  N1: Part1.CE, Part2.D10
  N2: Part1.CS, Part2.D9
  N3: Part1.SCK, Part2.D13/SCK
  N4: Part1.MOSI, Part2.D12/MISO
  N5: Part2.D6, S1.Pin_3, S1.Pin_4, C1.1
  5V: Part2.5V, S2.VCC
  N6: Part2.A5, S2.SCL
  N7: Part2.A4, S2.SDA
